# Fritzing sketch jcscpu-hmc (saved by Fritzing 0.9.4)
breadboards: 16

parts:
  Part1 = Arduino Nano (Rev3.0) (ICSP)
  Part2 = Arduino Nano (Rev3.0) (ICSP)
  R10 = Resistor [tolerance=±5% resistance=220 package="0402 [SMD]"]
  R11 = Resistor [tolerance=±5% resistance=220 package="0402 [SMD]"]
  R12 = Resistor [tolerance=±5% resistance=220 package="0402 [SMD]"]
  R13 = Resistor [tolerance=±5% resistance=220 package="0402 [SMD]"]
  R14 = Resistor [tolerance=±5% resistance=220 package="0402 [SMD]"]
  R15 = Resistor [tolerance=±5% resistance=220 package="0402 [SMD]"]
  R16 = Resistor [tolerance=±5% resistance=220 package="0402 [SMD]"]
  R17 = Resistor [tolerance=±5% resistance=220 package="0402 [SMD]"]
  LED16 = smd LED [color="Yellow (595nm)" package="1206 [SMD]"]
  LED17 = smd LED [color="Yellow (595nm)" package="1206 [SMD]"]
  LED18 = smd LED [color="Yellow (595nm)" package="1206 [SMD]"]
  U3 = 74HC595 [package="DIP16 [THT]"]  # not connected
  U4 = 74HC595 [package="DIP16 [THT]"]  # not connected
  U5 = 74HC595 [package="DIP16 [THT]"]
  U6 = 74HC595 [package="DIP16 [THT]"]
  U7 = 74HC595 [package="DIP16 [THT]"]
  U8 = 74HC595 [package="DIP16 [THT]"]
  U9 = 74HC595 [package="DIP16 [THT]"]
  U10 = 74HC595 [package="DIP16 [THT]"]
  U11 = 74HC595 [package="DIP16 [THT]"]
  U12 = 74HC595 [package="DIP16 [THT]"]
  U13 = 74HC595 [package="DIP16 [THT]"]
  U14 = 74HC595 [package="DIP16 [THT]"]
  U15 = 74HC595 [package="DIP16 [THT]"]
  U16 = 74HC595 [package="DIP16 [THT]"]
  Part3 = Arduino Nano (Rev3.0) (ICSP)
  LED23 = smd LED [color="Blue (505nm)" package="1206 [SMD]"]
  R18 = Resistor [tolerance=±5% resistance=220 package="0402 [SMD]"]
  R19 = Resistor [tolerance=±5% resistance=220 package="0402 [SMD]"]
  R20 = Resistor [tolerance=±5% resistance=220 package="0402 [SMD]"]
  R21 = Resistor [tolerance=±5% resistance=220 package="0402 [SMD]"]
  LED24 = smd LED [color="Blue (505nm)" package="1206 [SMD]"]
  LED25 = smd LED [color="Blue (505nm)" package="1206 [SMD]"]
  LED26 = smd LED [color="Blue (505nm)" package="1206 [SMD]"]
  Part4 = Arduino Nano (Rev3.0) (ICSP)
  LED27 = smd LED [color="Red (633nm)" package="1206 [SMD]"]
  LED28 = smd LED [color="Red (633nm)" package="1206 [SMD]"]
  LED29 = smd LED [color="Red (633nm)" package="1206 [SMD]"]
  LED30 = smd LED [color="Red (633nm)" package="1206 [SMD]"]
  LED31 = smd LED [color="Red (633nm)" package="1206 [SMD]"]
  LED32 = smd LED [color="Red (633nm)" package="1206 [SMD]"]
  R22 = Resistor [tolerance=±5% resistance=220 package="0402 [SMD]"]
  R23 = Resistor [tolerance=±5% resistance=220 package="0402 [SMD]"]
  R24 = Resistor [tolerance=±5% resistance=220 package="0402 [SMD]"]
  R25 = Resistor [tolerance=±5% resistance=220 package="0402 [SMD]"]
  R26 = Resistor [tolerance=±5% resistance=220 package="0402 [SMD]"]  # not connected
  R28 = Resistor [tolerance=±5% resistance=220 package="0402 [SMD]"]
  LED33 = smd LED [color="Red (633nm)" package="1206 [SMD]"]
  LED34 = smd LED [color="Red (633nm)" package="1206 [SMD]"]
  R29 = Resistor [tolerance=±5% resistance=220 package="0402 [SMD]"]
  LED36 = smd LED [color="Yellow (595nm)" package="1206 [SMD]"]
  LED37 = smd LED [color="Yellow (595nm)" package="1206 [SMD]"]
  LED38 = smd LED [color="Yellow (595nm)" package="1206 [SMD]"]
  LED39 = smd LED [color="Yellow (595nm)" package="1206 [SMD]"]
  Part5 = Arduino Nano (Rev3.0) (ICSP)
  SW1 = DIP Switch 8 Position [package=dipswitch-08]
  LED41 = smd LED [color="Green (555nm)" package="1206 [SMD]"]
  LED48 = smd LED [color="Yellow (595nm)" package="1206 [SMD]"]
  U21 = SN74LS32N [package="DIP14 [THT]"]  # not connected
  U22 = SN74LS32N [package="DIP14 [THT]"]  # not connected
  U23 = 74HC595 [package="DIP16 [THT]"]  # not connected
  U24 = 74HC595 [package="DIP16 [THT]"]  # not connected
  U25 = SN74LS32N [package="DIP14 [THT]"]  # not connected
  U26 = SN74LS32N [package="DIP14 [THT]"]  # not connected
  LED49 = smd LED [color="Red (633nm)" package="1206 [SMD]"]
  S1 = Pushbutton [package="[SMD]"]
  R30 = Resistor [tolerance=±5% resistance=10k package="0402 [SMD]"]
  U27 = SN74LS32N [package="DIP14 [THT]"]  # not connected
  U28 = 74HC595 [package="DIP16 [THT]"]  # not connected
  U29 = 74HC595 [package="DIP16 [THT]"]  # not connected
  U30 = 74HC595 [package="DIP16 [THT]"]  # not connected
  U31 = 74HC595 [package="DIP16 [THT]"]  # not connected
  R31 = Resistor [tolerance=±5% resistance=220 package="0402 [SMD]"]
  LED50 = smd LED [color="Yellow (595nm)" package="1206 [SMD]"]
  LED51 = smd LED [color="Yellow (595nm)" package="1206 [SMD]"]
  LED52 = smd LED [color="Yellow (595nm)" package="1206 [SMD]"]
  R32 = Resistor [tolerance=±5% resistance=10k package="0402 [SMD]"]
  R33 = Resistor [tolerance=±5% resistance=10k package="0402 [SMD]"]
  R34 = Resistor [tolerance=±5% resistance=10k package="0402 [SMD]"]
  R35 = Resistor [tolerance=±5% resistance=10k package="0402 [SMD]"]
  R36 = Resistor [tolerance=±5% resistance=10k package="0402 [SMD]"]
  R37 = Resistor [tolerance=±5% resistance=10k package="0402 [SMD]"]
  R38 = Resistor [tolerance=±5% resistance=10k package="0402 [SMD]"]
  R39 = Resistor [tolerance=±5% resistance=10k package="0402 [SMD]"]
  R5 = Resistor [tolerance=±5% resistance=1k package=THT]
  R7 = Resistor [tolerance=±5% resistance=1k package=THT]
  R6 = Resistor [tolerance=±5% resistance=1k package=THT]
  R4 = Resistor [tolerance=±5% resistance=1k package=THT]
  R3 = Resistor [tolerance=±5% resistance=1k package=THT]
  R2 = Resistor [tolerance=±5% resistance=1k package=THT]
  R8 = Resistor [tolerance=±5% resistance=1k package=THT]
  R1 = Resistor [tolerance=±5% resistance=1k package=THT]
  R27 = Resistor [tolerance=±5% resistance=1k package=THT]
  LED53 = smd LED [color="Green (555nm)" package="1206 [SMD]"]
  LED54 = smd LED [color="Green (555nm)" package="1206 [SMD]"]
  LED55 = smd LED [color="Green (555nm)" package="1206 [SMD]"]
  LED56 = smd LED [color="Green (555nm)" package="1206 [SMD]"]
  LED57 = smd LED [color="Green (555nm)" package="1206 [SMD]"]
  LED58 = smd LED [color="Green (555nm)" package="1206 [SMD]"]
  LED59 = smd LED [color="Green (555nm)" package="1206 [SMD]"]

nets:
  N1: Part1.D1/TX, Part5.D1/TX
  N2: Part1.D0/RX, Part5.D0/RX
  N3: Part1.RESET, Part5.RESET
  GND: Part1.GND, Part5.GND
  N4: Part1.D2, Part5.D2
  N5: Part1.D3, Part5.D3
  N6: Part1.D4, Part5.D4
  VCC: Part1.D5, U5.Q3, U6.Q1, U7.DS, U7.Q0, U8.VCC, U9.VCC, U10.DS, U10.Q0, U13.Q1, U14.Q2, U14.Q3, Part5.D5, SW1.9, LED41.anode, R38.Pin_0
  N7: Part1.D6, U5.Q4, U6.Q2, U7.ST_CP, U7.OE, U8.DS, U8.Q0, U9.DS, U9.Q0, U10.ST_CP, U10.OE, U13.Q2, U13.Q3, U14.Q4, U14.Q5, Part5.D6, SW1.10, R37.Pin_0, LED53.anode
  N8: Part1.D7, U5.Q7, U6.Q5, U9.ST_CP, U9.OE, U10.MR, U10.SH_CP, U13.Q4, U13.Q5, U14.Q6, U14.Q7, Part5.D7, SW1.11, R39.Pin_0, LED54.anode
  GND_2: Part1.D8, U5.GND, U6.Q6, U9.MR, U9.SH_CP, U10.Q7', U13.Q6, U13.Q7, U14.GND, Part5.D8, SW1.12, R36.Pin_0, LED55.anode
  GND_3: Part1.D9, U9.Q6, U9.Q7, U10.GND, U11.Q6, U11.Q7, U12.GND, Part5.D9, SW1.13, R34.Pin_0, LED56.anode
  N9: Part1.D10, U9.Q4, U9.Q5, U10.Q6, U10.Q7, U11.Q4, U11.Q5, U12.Q6, U12.Q7, Part5.D10, SW1.14, R35.Pin_0, LED57.anode
  N10: Part1.D11/MOSI, U5.OE, U6.Q0, U9.Q3, U10.Q5, U11.Q2, U11.Q3, U12.Q4, U12.Q5, Part5.D11/MOSI, SW1.15, R33.Pin_0, LED59.anode
  N11: Part1.D12/MISO, U5.DS, U6.VCC, U10.Q2, U12.Q2, Part5.D12/MISO, SW1.16, R32.Pin_0, LED58.anode
  VIN: Part1.VIN, Part5.VIN
  5V: Part1.5V, Part5.5V
  N12: Part1.A7, Part5.A7
  N13: Part1.A6, Part5.A6
  N14: Part1.A5, Part2.A5, Part3.A5, Part4.A5, Part5.A5
  N15: Part1.A4, Part2.A4, Part3.A4, Part4.A4, Part5.A4
  N16: Part1.A3, Part5.A3
  N17: Part1.A2, Part5.A2
  N18: Part1.A1, Part5.A1
  N19: Part1.A0, Part5.A0
  N20: Part1.AREF, Part5.AREF
  3V3: Part1.3V3, Part5.3V3
  N21: Part1.D13/SCK, Part5.D13/SCK
  N22: Part2.D5, LED37.anode
  N23: Part2.D6, U5.Q5, U6.Q3, LED39.anode
  N24: Part2.D7, LED38.anode
  N25: Part2.D8, LED36.anode
  N26: Part2.D9, LED18.anode, LED50.anode
  N27: Part2.D10, LED17.anode, U5.SH_CP, U6.OE
  N28: Part2.D11/MOSI, LED16.anode, U5.ST_CP, U6.DS, LED51.anode
  N29: Part2.D12/MISO, U5.Q0, LED48.anode, LED52.anode
  N30: R10.Pin_0, R11.Pin_0, R12.Pin_0, R13.Pin_0, R14.Pin_0, R15.Pin_0, R16.Pin_0, R17.Pin_0, R32.Pin_1, R33.Pin_1, R34.Pin_1, R35.Pin_1, R36.Pin_1, R37.Pin_1, R38.Pin_1, R5.Pin_0, R7.Pin_0, R6.Pin_0, R4.Pin_0, R3.Pin_0, R2.Pin_0, R8.Pin_0, R1.Pin_0
  N31: R10.Pin_1, LED37.cathode
  N32: R11.Pin_1, LED39.cathode
  N33: R12.Pin_1, LED18.cathode, LED50.cathode
  N34: R13.Pin_1, LED38.cathode
  N35: R14.Pin_1, LED36.cathode
  N36: R15.Pin_1, LED17.cathode
  N37: R16.Pin_1, LED16.cathode, LED51.cathode
  N38: R17.Pin_1, LED48.cathode, LED52.cathode
  N39: U5.Q6, U6.Q4
  N40: U5.Q7', U6.SH_CP
  N41: U5.MR, U6.ST_CP
  N42: U7.Q2, U7.Q3, U8.Q1
  N43: U7.Q4, U7.Q5, U8.Q2, U8.Q3
  N44: U7.Q6, U7.Q7, U8.Q4, U8.Q5
  N45: U7.GND, U8.Q6, U8.Q7
  N46: U7.Q7', U8.MR, U8.SH_CP
  N47: U7.MR, U7.SH_CP, U8.ST_CP, U8.OE
  VCC_2: U7.VCC, U10.VCC, S1.Pin_3, S1.Pin_4
  GND_4: U8.GND, U9.GND, U11.GND, U13.GND, U15.GND, R22.Pin_0, R23.Pin_0, R24.Pin_0, R25.Pin_0, R28.Pin_0, R29.Pin_0, R30.Pin_0, R31.Pin_0, R27.Pin_0
  N48: U9.Q1, U10.Q3
  N49: U9.Q2, U10.Q4
  N50: U11.Q1, U12.Q3
  N51: U11.SH_CP, U12.Q7'
  N52: U11.OE, U12.SH_CP
  N53: U11.DS, U12.ST_CP
  N54: U11.Q0, U12.OE
  N55: U11.VCC, U12.DS
  N56: U13.SH_CP, U14.Q7'
  N57: U13.ST_CP, U14.MR
  N58: U13.OE, U14.SH_CP
  N59: U13.DS, U14.ST_CP
  N60: U13.Q0, U14.OE
  N61: U13.VCC, U14.DS
  N62: U15.Q1, U16.Q3, Part3.D5
  N63: U15.Q2, U16.Q4, Part3.D4
  N64: U15.Q3, U16.Q5, LED23.anode
  N65: U15.Q4, U16.Q6, LED25.anode
  N66: U15.Q5, U16.Q7, Part3.D3
  N67: U15.Q6, U16.GND, Part3.D2
  N68: U15.Q7, LED24.anode
  N69: U15.SH_CP, U16.Q7'
  N70: U15.ST_CP, U16.MR
  N71: U15.OE, U16.SH_CP
  N72: U15.DS, U16.ST_CP
  N73: U15.Q0, U16.OE
  N74: U15.VCC, U16.DS
  N75: U16.Q2, LED26.anode
  N76: LED23.cathode, R21.Pin_0
  N77: R18.Pin_0, LED24.cathode
  N78: R18.Pin_1, R19.Pin_1, R20.Pin_1, R21.Pin_1
  N79: R19.Pin_0, LED26.cathode
  N80: R20.Pin_0, LED25.cathode
  N81: Part4.D2, LED27.anode
  N82: Part4.D3, LED32.anode
  N83: Part4.D4, LED31.anode
  N84: Part4.D5, LED30.anode
  N85: Part4.D6, LED29.anode
  N86: Part4.D7, LED28.anode
  N87: Part4.D8, LED33.anode
  N88: Part4.D9, LED34.anode
  N89: Part4.D10, S1.Pin_1, S1.Pin_2, R30.Pin_1
  N90: Part4.D11/MOSI, LED49.anode
  N91: R28.Pin_1, LED33.cathode
  N92: LED34.cathode, R29.Pin_1
  N93: SW1.1, SW1.2, SW1.3, SW1.4, SW1.5, SW1.6, SW1.7, SW1.8
  N94: LED41.cathode, R6.Pin_1
  N95: LED49.cathode, R31.Pin_1
  N96: R7.Pin_1, LED53.cathode
  N97: R4.Pin_1, LED55.cathode
  N98: R3.Pin_1, LED56.cathode
  N99: R2.Pin_1, LED57.cathode
  N100: R8.Pin_1, LED59.cathode
  N101: R1.Pin_1, LED58.cathode

notes:
  RAM_e, RAM_s, MAR_e, HLT_e
  IAR_e, IAR_s, IR_s
  ALU0, ALU1, ALU2, JX
  FLAGS_s, Ctmp_e
  TMP_s, ACC_e, ACC_s, BUS1
  R0_e, R0_s, R1_e, R1_s
  IO_e, IO_s, IO_d, IO_a
  R2_e, R2_s, R3_e, R3_s
